// Logisim project increment1ikenSayanSayici.circ as structural Verilog: 1 circuit, main circuit main
module main (
  input  increment,
  input  in_2,
  input  in_3,
  input  in_4
);

  wire and_1_out, and_2_out, clock_1_out, d_ff_1_q, t_ff_1_q, xor_1_out;

  Clock clock_1 (.out(clock_1_out));
  and and_1 (and_1_out, increment, d_ff_1_q, t_ff_1_q);
  J_K_Flip_Flop j_k_ff_1 (
    .J(and_1_out), .clk(clock_1_out), .K(and_1_out), .preset(in_2), .en(in_3), .reset(in_4));  // open: Q, Qn
  T_Flip_Flop t_ff_1 (
    .clk(clock_1_out), .T(and_2_out), .Q(t_ff_1_q), .preset(in_2), .reset(in_4), .en(in_3));  // open: Qn
  and and_2 (and_2_out, d_ff_1_q, increment);
  xor xor_1 (xor_1_out, increment, d_ff_1_q);
  D_Flip_Flop d_ff_1 (
    .clk(clock_1_out), .D(xor_1_out), .Q(d_ff_1_q), .preset(in_2), .en(in_3), .reset(in_4));  // open: Qn

  // Notes on the sheet:
  //   increment 1 iken sayan sayıcı
endmodule
