// Logisim project logicGates Transistor.circ as structural Verilog: 1 circuit, main circuit main
module main (
  input  in_1,
  input  in_2,
  input  in_3,
  input  in_4,
  input  in_5,
  input  in_6,
  input  in_7,
  input  in_8
);

  wire transistor_1_out, transistor_2_out, transistor_3_out, transistor_4_out, transistor_5_out,
       transistor_6_out, transistor_7_out, transistor_8_out, transistor_9_out, transistor_10_out;

  // NAND_Gate nand_1 is placed but not wired
  Transistor transistor_1 (.in(1'b1), .out(transistor_1_out), .gate(in_5));
  Transistor transistor_2 (.in(transistor_1_out), .out(transistor_2_out), .gate(in_7));
  LED led_1 (.in(transistor_2_out));
  Transistor #(.\type ("n")) transistor_3 (.in(transistor_2_out), .out(transistor_3_out), .gate(in_5));
  Transistor #(.\type ("n")) transistor_4 (.in(transistor_3_out), .out(transistor_4_out), .gate(in_7));
  Transistor #(.\type ("n")) transistor_5 (.in(1'b1), .out(transistor_5_out), .gate(in_3));
  Transistor #(.\type ("n")) transistor_6 (.in(transistor_5_out), .out(transistor_6_out), .gate(in_4));
  LED led_2 (.in(transistor_6_out));
  Pull_Resistor pull_resistor_1 (.node(transistor_6_out));
  // NOR_Gate nor_1 is placed but not wired
  Transistor #(.\type ("n")) transistor_7 (.in(transistor_10_out), .out(transistor_7_out), .gate(in_6));
  Transistor #(.\type ("n")) transistor_8 (.in(1'b1), .out(transistor_8_out), .gate(in_1));
  Pull_Resistor pull_resistor_2 (.node(transistor_8_out));
  Transistor transistor_9 (.in(1'b1), .out(transistor_9_out), .gate(in_6));
  Transistor transistor_10 (.in(transistor_9_out), .out(transistor_10_out), .gate(in_8));
  LED led_3 (.in(transistor_10_out));
  Transistor #(.\type ("n")) transistor_11 (.in(transistor_10_out), .out(transistor_7_out), .gate(in_8));
  Transistor #(.\type ("n")) transistor_12 (.in(1'b1), .out(transistor_8_out), .gate(in_2));
  LED led_4 (.in(transistor_8_out));
  // also tied to GND on the sheet: {transistor_4_out, transistor_7_out}

  // Notes on the sheet:
  //   NAND GATE
  //   AND GATE
  //   NOR GATE
  //   OR GATE
endmodule
