// Logisim project sayıcılar (genisletme).circ as structural Verilog: 1 circuit, main circuit main
module main (
  input  in_1,
  input  in_2,
  input  in_3,
  output out_4,
  output out_5,
  output out_6,
  output out_7
);

  wire and_1_out, and_2_out, clock_1_out;

  Clock clock_1 (.out(clock_1_out));
  Hex_Digit_Display hex_digit_display_1 (.value({out_4, out_5, out_6, out_7}), .dp(in_2));
  J_K_Flip_Flop j_k_ff_1 (
    .J(and_1_out), .clk(clock_1_out), .K(and_1_out), .Q(out_4), .preset(in_1), .en(in_2));  // open: Qn, reset
  and and_1 (and_1_out, and_2_out, out_5);
  J_K_Flip_Flop j_k_ff_2 (
    .J(and_2_out), .clk(clock_1_out), .K(and_2_out), .Q(out_5), .preset(in_1), .en(in_2), .reset(in_3));  // open: Qn
  and and_2 (and_2_out, out_7, out_6);
  J_K_Flip_Flop j_k_ff_3 (
    .J(out_7), .clk(clock_1_out), .K(out_7), .Q(out_6), .preset(in_1), .en(in_2), .reset(in_3));  // open: Qn
  J_K_Flip_Flop j_k_ff_4 (
    .J(1'b1), .clk(clock_1_out), .K(1'b1), .Q(out_7), .preset(in_1), .en(in_2), .reset(in_3));  // open: Qn

  // Notes on the sheet:
  //   4 Bitlik senkson sayıcı
  //   Genişletme ucu
  //   Genişletme ucu
  //   Genişletme ucu
endmodule
