// Logisim project senkron sayıcılar.circ as structural Verilog: 1 circuit, main circuit main
module main (
  input  in_1,
  input  in_2,
  input  in_3,
  input  in_4,
  input  in_5,
  input  in_6,
  input  in_7,
  input  in_8,
  input  in_9,
  output out_10,
  output out_11,
  output out_12,
  output out_13,
  output out_14,
  output out_15
);

  wire and_1_out, clock_1_out, clock_2_out, clock_3_out;

  Clock clock_1 (.out(clock_1_out));
  Clock clock_2 (.out(clock_2_out));
  and and_1 (and_1_out, out_14, out_15);
  J_K_Flip_Flop j_k_ff_1 (
    .J(1'b1), .clk(clock_1_out), .K(1'b1), .Q(out_10), .preset(in_3), .en(in_5), .reset(in_1));  // open: Qn
  J_K_Flip_Flop j_k_ff_2 (
    .J(and_1_out), .clk(clock_2_out), .K(and_1_out), .Q(out_13), .preset(in_7), .en(in_9), .reset(in_8));  // open: Qn
  Clock clock_3 (.out(clock_3_out));
  J_K_Flip_Flop j_k_ff_3 (
    .J(out_15), .clk(clock_2_out), .K(out_15), .Q(out_14), .preset(in_7), .en(in_9), .reset(in_8));  // open: Qn
  J_K_Flip_Flop j_k_ff_4 (
    .J(out_12), .clk(clock_3_out), .K(out_12), .Q(out_11), .preset(in_2), .en(in_6), .reset(in_4));  // open: Qn
  J_K_Flip_Flop j_k_ff_5 (
    .J(1'b1), .clk(clock_2_out), .K(1'b1), .Q(out_15), .preset(in_8), .en(in_9), .reset(in_7));  // open: Qn
  J_K_Flip_Flop j_k_ff_6 (
    .J(1'b1), .clk(clock_3_out), .K(1'b1), .Q(out_12), .preset(in_4), .en(in_6), .reset(in_2));  // open: Qn

  // Notes on the sheet:
  //   1Bitlik senkron sayıcı
  //   3Bitlik senkron sayıcı
  //   2Bitlik senkron sayıcı
endmodule
