// Logisim project son 3 girişi 1 olan(moore).circ as structural Verilog: 1 circuit, main circuit main
module main (
  input  x,
  input  in_2,
  input  in_3,
  input  in_4
);

  wire and_1_out, and_2_out, clock_1_out, j_k_ff_1_q, j_k_ff_1_qn, j_k_ff_2_q, not_1_out, or_1_out;

  not not_1 (not_1_out, x);
  Clock clock_1 (.out(clock_1_out));
  and and_1 (and_1_out, j_k_ff_2_q, x);
  J_K_Flip_Flop j_k_ff_1 (
    .J(and_1_out), .clk(clock_1_out), .K(not_1_out), .Q(j_k_ff_1_q), .Qn(j_k_ff_1_qn), .preset(in_2),
    .en(in_4), .reset(in_3));
  or or_1 (or_1_out, not_1_out, j_k_ff_1_qn);
  J_K_Flip_Flop j_k_ff_2 (
    .J(x), .clk(clock_1_out), .K(or_1_out), .Q(j_k_ff_2_q), .preset(in_2), .en(in_4), .reset(in_3));  // open: Qn
  and and_2 (and_2_out, j_k_ff_2_q, j_k_ff_1_q);
  LED led_1 (.in(and_2_out));

  // Notes on the sheet:
  //   z
endmodule
